// Logisim project CPU.circ as structural Verilog: 11 circuits, main circuit main
module main (
  input  in_1,
  output [11:0] out_2,
  output [11:0] out_3,
  output [15:0] out_4,
  output out_5,
  output [15:0] out_6,
  output [15:0] out_7,
  output [15:0] out_8
);

  wire clock_1_out, clock_2_out_2, clock_2_out_3, clock_2_out_4, controlled_buffer_1_out, cu_1_ace, cu_1_acs,
       cu_1_ar_plus_plus, cu_1_are, cu_1_ars, cu_1_cla, cu_1_cle, cu_1_dec, cu_1_dr_plus_plus, cu_1_dre,
       cu_1_drs, cu_1_ire, cu_1_irs, cu_1_ldafalu1, cu_1_ldafalu2c, cu_1_me, cu_1_ms, cu_1_out_30,
       cu_1_pc_plus_plus, cu_1_pce, cu_1_pcs, cu_1_tmpe, cu_1_tmps, not_1_out;
  wire [2:0] cu_1_out_32;
  wire [11:0] ar_1_out_8, controlled_buffer_2_out, controlled_buffer_3_out, controlled_buffer_6_out,
       pc_1_out_8;
  wire [15:0] ac_1_out_8, alu1_1_out_8, controlled_buffer_4_out, controlled_buffer_9_out,
       controlled_buffer_10_out, controlled_buffer_13_out, cu_1_out_31, dr_1_out_8, ir_1_out_8, tmp_1_out_6;
  wire [15:12] controlled_buffer_3_out_2;

  ALU1 alu1_1 (
    .in_1(out_7), .in_2(out_8), .out_8(alu1_1_out_8), .out_9(out_5), .in_3(cu_1_out_32),
    .in_4(cu_1_ldafalu1), .in_5(cu_1_cle), .in_7(cu_1_out_31), .in_6(cu_1_ldafalu2c));
  Clock clock_1 (.out(clock_1_out));
  assign controlled_buffer_1_out = not_1_out ? clock_1_out : 1'bz;  // Controlled_Buffer controlled_buffer_1
  not not_1 (not_1_out, cu_1_out_30);
  CLOCK clock_2 (.in_1(controlled_buffer_1_out), .out_2(clock_2_out_2), .out_3(clock_2_out_3), .out_4(clock_2_out_4));
  assign controlled_buffer_2_out = cu_1_pcs ? controlled_buffer_3_out : 12'bz;  // Controlled_Buffer controlled_buffer_2
  assign {controlled_buffer_3_out_2, controlled_buffer_3_out} = cu_1_ace ? ac_1_out_8 : 16'bz;  // Controlled_Buffer controlled_buffer_3
  AC ac_1 (
    .in_1(alu1_1_out_8), .in_2(controlled_buffer_4_out), .in_3(clock_2_out_3), .in_4(cu_1_cla),
    .in_6(cu_1_ace), .out_7(out_8), .out_8(ac_1_out_8), .in_5(cu_1_acs));
  PC pc_1 (
    .in_2(controlled_buffer_2_out), .in_3(clock_2_out_3), .in_4(in_1), .out_7(out_2), .out_8(pc_1_out_8),
    .in_6(cu_1_pce), .in_5(cu_1_pcs), .in_1(cu_1_pc_plus_plus));
  assign controlled_buffer_4_out = cu_1_acs ? {controlled_buffer_3_out_2, controlled_buffer_3_out} : 16'bz;  // Controlled_Buffer controlled_buffer_4
  assign controlled_buffer_3_out = cu_1_pce ? pc_1_out_8 : 12'bz;  // Controlled_Buffer controlled_buffer_5
  assign controlled_buffer_6_out = cu_1_ars ? controlled_buffer_3_out : 12'bz;  // Controlled_Buffer controlled_buffer_6
  assign {controlled_buffer_3_out_2, controlled_buffer_3_out} = cu_1_ire ? ir_1_out_8 : 16'bz;  // Controlled_Buffer controlled_buffer_7
  AR ar_1 (
    .in_2(controlled_buffer_6_out), .in_3(clock_2_out_3), .out_7(out_3), .out_8(ar_1_out_8), .in_4(cu_1_ars),
    .in_6(cu_1_are), .in_1(cu_1_ar_plus_plus));  // open: in_5
  IR ir_1 (
    .in_2(controlled_buffer_9_out), .in_3(cu_1_irs), .in_4(clock_2_out_3), .in_6(cu_1_ire), .out_7(out_6),
    .out_8(ir_1_out_8), .in_1(cu_1_dec));  // open: in_5
  assign controlled_buffer_3_out = cu_1_are ? ar_1_out_8 : 12'bz;  // Controlled_Buffer controlled_buffer_8
  CU cu_1 (
    .S(clock_2_out_3), .in_3(clock_2_out_2), .E(clock_2_out_4), .ARS(cu_1_ars), .IRS(cu_1_irs),
    .PCE(cu_1_pce), .ME(cu_1_me), .ACS(cu_1_acs), .PCS(cu_1_pcs), .ARE(cu_1_are), .MS(cu_1_ms),
    .ACE(cu_1_ace), .IRE(cu_1_ire), .DRS(cu_1_drs), .DRE(cu_1_dre), .in_7(out_6), .out_32(cu_1_out_32),
    .LDAFALU1(cu_1_ldafalu1), .TMPE(cu_1_tmpe), .TMPS(cu_1_tmps), .PC_plus_plus(cu_1_pc_plus_plus),
    .DEC(cu_1_dec), .AR_plus_plus(cu_1_ar_plus_plus), .DR_plus_plus(cu_1_dr_plus_plus), .in_6(out_7),
    .out_31(cu_1_out_31), .CLA(cu_1_cla), .CLE(cu_1_cle), .LDAFALU2C(cu_1_ldafalu2c), .in_4(out_8),
    .in_5(out_5), .out_30(cu_1_out_30));
  assign controlled_buffer_9_out = cu_1_irs ? {controlled_buffer_3_out_2, controlled_buffer_3_out} : 16'bz;  // Controlled_Buffer controlled_buffer_9
  assign controlled_buffer_10_out = cu_1_tmps ? {controlled_buffer_3_out_2, controlled_buffer_3_out} : 16'bz;  // Controlled_Buffer controlled_buffer_10
  assign {controlled_buffer_3_out_2, controlled_buffer_3_out} = cu_1_dre ? dr_1_out_8 : 16'bz;  // Controlled_Buffer controlled_buffer_11
  assign {controlled_buffer_3_out_2, controlled_buffer_3_out} = cu_1_tmpe ? tmp_1_out_6 : 16'bz;  // Controlled_Buffer controlled_buffer_12
  TMP tmp_1 (
    .in_1(controlled_buffer_10_out), .in_2(cu_1_tmpe), .in_3(cu_1_tmps), .in_4(clock_2_out_3),
    .out_6(tmp_1_out_6), .out_5(out_4));
  DR dr_1 (
    .out_7(out_7), .in_2(controlled_buffer_13_out), .out_8(dr_1_out_8), .in_3(clock_2_out_3),
    .in_5(cu_1_drs), .in_6(cu_1_dre), .in_1(cu_1_dr_plus_plus));  // open: in_4
  assign controlled_buffer_13_out = cu_1_drs ? {controlled_buffer_3_out_2, controlled_buffer_3_out} : 16'bz;  // Controlled_Buffer controlled_buffer_13
  RAM #(.addrWidth(12), .dataWidth(16), .bus("separate")) ram_1 (
    .addr(out_3), .din({controlled_buffer_3_out_2, controlled_buffer_3_out}),
    .data({controlled_buffer_3_out_2, controlled_buffer_3_out}), .str(cu_1_ms), .clk(cu_1_ms), .ld(cu_1_me));  // open: sel, clr

  // Notes on the sheet:
  //   out_4: pull=down
endmodule

module DR (
  input  in_1,
  input  [15:0] in_2,
  input  in_3,
  input  in_4,
  input  in_5,
  input  in_6,
  output [15:0] out_7,
  output [15:0] out_8
);

  wire [15:0] adder_1_out, controlled_buffer_1_out, controlled_buffer_2_out;

  Adder #(.width(16)) adder_1 (.a(controlled_buffer_2_out), .b(16'h1), .out(adder_1_out));  // open: cin, cout
  assign controlled_buffer_1_out = in_5 ? in_2 : 16'bz;  // Controlled_Buffer controlled_buffer_1
  assign controlled_buffer_2_out = in_1 ? out_7 : 16'bz;  // Controlled_Buffer controlled_buffer_2
  assign controlled_buffer_1_out = in_1 ? adder_1_out : 16'bz;  // Controlled_Buffer controlled_buffer_3
  Register #(.width(16), .trigger("falling")) register_1 (
    .D(controlled_buffer_1_out), .Q(out_7), .clk(in_3), .clr(in_4));  // open: en
  assign out_8 = in_6 ? out_7 : 16'bz;  // Controlled_Buffer controlled_buffer_4

  // Notes on the sheet:
  //   in_1: pull=down
  //   in_6: pull=down
  //   in_4: pull=down
endmodule

module CU (
  input  S,
  input  E,
  input  in_3,
  input  [15:0] in_4,
  input  in_5,
  input  [15:0] in_6,
  input  [15:0] in_7,
  output PCS,
  output PCE,
  output ME,
  output MS,
  output ARS,
  output ARE,
  output IRS,
  output IRE,
  output ACE,
  output ACS,
  output DRS,
  output DRE,
  output LDAFALU1,
  output PC_plus_plus,
  output DEC,
  output AR_plus_plus,
  output DR_plus_plus,
  output CLA,
  output CLE,
  output LDAFALU2C,
  output TMPS,
  output TMPE,
  output out_30,
  output [15:0] out_31,
  output [2:0] out_32
);

  wire and_1_out, and_2_out, and_3_out, and_6_out, comparator_1_eq, comparator_2_eq, comparator_3_eq,
       comparator_4_eq, comparator_5_eq, comparator_6_eq, comparator_7_eq, comparator_8_eq, comparator_9_eq,
       comparator_10_eq, comparator_11_eq, comparator_12_eq, comparator_13_eq, comparator_14_eq,
       demultiplexer_1_out0, demultiplexer_1_out1, demultiplexer_2_out0, demultiplexer_2_out1,
       demultiplexer_3_out0, demultiplexer_4_out0, demultiplexer_4_out1, demultiplexer_4_out2,
       demultiplexer_4_out3, demultiplexer_4_out4, demultiplexer_4_out5, demultiplexer_4_out6,
       demultiplexer_4_out7, demultiplexer_4_out8, demultiplexer_4_out9, demultiplexer_4_out10,
       demultiplexer_5_out1, demultiplexer_6_out1, demultiplexer_7_out1, demultiplexer_8_out1,
       demultiplexer_9_out0, demultiplexer_9_out1, demultiplexer_9_out2, demultiplexer_9_out3,
       demultiplexer_9_out4, demultiplexer_9_out5, demultiplexer_9_out6, demultiplexer_10_out0,
       demultiplexer_10_out1, demultiplexer_10_out2, demultiplexer_10_out3, demultiplexer_10_out4,
       demultiplexer_10_out5, demultiplexer_10_out6, demultiplexer_11_out0, demultiplexer_11_out1, not_1_out,
       not_2_out, not_3_out, not_4_out, not_5_out, not_6_out, not_7_out, not_8_out, not_9_out, not_10_out,
       not_11_out, not_12_out, not_13_out, not_14_out, not_15_out, not_16_out, not_17_out, not_18_out,
       not_19_out, not_20_out, not_21_out, not_22_out, not_23_out, not_24_out, not_25_out, or_1_out,
       or_2_out, or_3_out, or_4_out, or_5_out, or_6_out, or_7_out, or_8_out, or_9_out, or_10_out, or_11_out,
       or_12_out, or_13_out;
  wire [3:0] table_1_out_2;
  wire [7:0] counter_1_q;

  Counter #(.trigger("falling")) counter_1 (
    .Q(counter_1_q), .clk(in_3), .clr(or_1_out));  // open: load, D, count, carry
  or or_1 (or_1_out, demultiplexer_2_out1, demultiplexer_11_out0, comparator_8_eq, demultiplexer_10_out3, demultiplexer_10_out4);
  Comparator comparator_1 (.a(counter_1_q), .b({8{1'b0}}), .eq(comparator_1_eq));  // open: gt, lt
  Comparator comparator_2 (.a(counter_1_q), .b(8'h1), .eq(comparator_2_eq));  // open: gt, lt
  Comparator comparator_3 (.a(counter_1_q), .b(8'h2), .eq(comparator_3_eq));  // open: gt, lt
  Comparator comparator_4 (.a(counter_1_q), .b(8'h3), .eq(comparator_4_eq));  // open: gt, lt
  Comparator comparator_5 (.a(counter_1_q), .b(8'h4), .eq(comparator_5_eq));  // open: gt, lt
  Comparator comparator_6 (.a(counter_1_q), .b(8'h5), .eq(comparator_6_eq));  // open: gt, lt
  Comparator comparator_7 (.a(counter_1_q), .b(8'h6), .eq(comparator_7_eq));  // open: gt, lt
  Comparator comparator_8 (.a(counter_1_q), .b(8'h7), .eq(comparator_8_eq));  // open: gt, lt
  TABLE table_1 (.in_1(in_7), .out_2(table_1_out_2));
  Demultiplexer demultiplexer_1 (
    .out0(demultiplexer_1_out0), .out1(demultiplexer_1_out1), .in(comparator_4_eq), .sel(and_3_out));  // open: en
  Demultiplexer #(.disabled(0)) demultiplexer_2 (
    .out0(demultiplexer_2_out0), .out1(demultiplexer_2_out1), .in(comparator_5_eq), .sel(and_1_out));  // open: en
  Demultiplexer #(.disabled(0)) demultiplexer_3 (
    .out0(demultiplexer_3_out0), .in(comparator_6_eq), .sel(and_1_out));  // open: out1, en
  assign PCS = not_1_out ? 1'b0 : 1'bz;  // Controlled_Buffer controlled_buffer_1
  not not_1 (not_1_out, or_2_out);
  assign PCS = or_2_out ? S : 1'bz;  // Controlled_Buffer controlled_buffer_2
  or or_2 (or_2_out, demultiplexer_9_out4, demultiplexer_10_out5);
  Comparator #(.width(3)) comparator_9 (.a(in_7[14:12]), .b(3'b111), .eq(comparator_9_eq));  // open: gt, lt
  not not_2 (not_2_out, in_7[15]);
  Comparator #(.width(3)) comparator_10 (.a(in_7[14:12]), .b(3'b111), .eq(comparator_10_eq));  // open: gt, lt
  Comparator #(.width(3)) comparator_11 (.a(in_7[14:12]), .b(3'b111), .eq(comparator_11_eq));  // open: gt, lt
  assign PCE = not_3_out ? 1'b0 : 1'bz;  // Controlled_Buffer controlled_buffer_3
  not not_3 (not_3_out, or_3_out);
  assign PCE = or_3_out ? E : 1'bz;  // Controlled_Buffer controlled_buffer_4
  not not_4 (not_4_out, comparator_11_eq);
  or or_3 (or_3_out, comparator_1_eq, demultiplexer_9_out5);
  and and_1 (and_1_out, comparator_9_eq, not_2_out);
  and and_2 (and_2_out, comparator_10_eq, in_7[15]);
  and and_3 (and_3_out, not_4_out, in_7[15]);
  assign ME = not_5_out ? 1'b0 : 1'bz;  // Controlled_Buffer controlled_buffer_5
  not not_5 (not_5_out, or_4_out);
  assign ME = or_4_out ? E : 1'bz;  // Controlled_Buffer controlled_buffer_6
  or or_4 (or_4_out, comparator_2_eq, demultiplexer_1_out1, demultiplexer_9_out0, demultiplexer_9_out1, demultiplexer_9_out2, demultiplexer_9_out6);
  assign MS = not_6_out ? 1'b0 : 1'bz;  // Controlled_Buffer controlled_buffer_7
  or or_5 (or_5_out, and_1_out, and_3_out, and_2_out);
  not not_6 (not_6_out, or_6_out);
  assign MS = or_6_out ? S : 1'bz;  // Controlled_Buffer controlled_buffer_8
  or or_6 (or_6_out, demultiplexer_9_out3, demultiplexer_9_out5, comparator_7_eq);
  not not_7 (not_7_out, or_5_out);
  assign ARS = not_8_out ? 1'b0 : 1'bz;  // Controlled_Buffer controlled_buffer_9
  not not_8 (not_8_out, or_7_out);
  assign ARS = or_7_out ? S : 1'bz;  // Controlled_Buffer controlled_buffer_10
  or or_7 (or_7_out, comparator_1_eq, comparator_3_eq, demultiplexer_1_out1);
  assign ARE = not_9_out ? 1'b0 : 1'bz;  // Controlled_Buffer controlled_buffer_11
  not not_9 (not_9_out, or_8_out);
  assign ARE = or_8_out ? E : 1'bz;  // Controlled_Buffer controlled_buffer_12
  or or_8 (or_8_out, demultiplexer_9_out4, demultiplexer_10_out5);
  assign IRS = not_10_out ? 1'b0 : 1'bz;  // Controlled_Buffer controlled_buffer_13
  not not_10 (not_10_out, comparator_2_eq);
  assign IRS = comparator_2_eq ? S : 1'bz;  // Controlled_Buffer controlled_buffer_14
  assign IRE = not_11_out ? 1'b0 : 1'bz;  // Controlled_Buffer controlled_buffer_15
  not not_11 (not_11_out, comparator_3_eq);
  assign IRE = comparator_3_eq ? E : 1'bz;  // Controlled_Buffer controlled_buffer_16
  assign ACE = not_12_out ? 1'b0 : 1'bz;  // Controlled_Buffer controlled_buffer_17
  not not_12 (not_12_out, demultiplexer_9_out3);
  assign ACE = demultiplexer_9_out3 ? E : 1'bz;  // Controlled_Buffer controlled_buffer_18
  assign ACS = not_13_out ? 1'b0 : 1'bz;  // Controlled_Buffer controlled_buffer_19
  not not_13 (not_13_out, demultiplexer_10_out2);
  assign ACS = demultiplexer_10_out2 ? S : 1'bz;  // Controlled_Buffer controlled_buffer_20
  assign DRS = not_14_out ? 1'b0 : 1'bz;  // Controlled_Buffer controlled_buffer_21
  not not_14 (not_14_out, or_9_out);
  assign DRS = or_9_out ? S : 1'bz;  // Controlled_Buffer controlled_buffer_22
  or or_9 (or_9_out, demultiplexer_9_out0, demultiplexer_9_out1, demultiplexer_9_out2, demultiplexer_9_out6);
  assign DRE = not_15_out ? 1'b0 : 1'bz;  // Controlled_Buffer controlled_buffer_23
  not not_15 (not_15_out, or_10_out);
  assign DRE = or_10_out ? E : 1'bz;  // Controlled_Buffer controlled_buffer_24
  or or_10 (or_10_out, demultiplexer_10_out2, comparator_7_eq);
  assign LDAFALU1 = not_16_out ? 1'b0 : 1'bz;  // Controlled_Buffer controlled_buffer_25
  assign LDAFALU1 = or_11_out ? S : 1'bz;  // Controlled_Buffer controlled_buffer_26
  not not_16 (not_16_out, or_11_out);
  or or_11 (or_11_out, demultiplexer_10_out0, demultiplexer_10_out1);
  assign PC_plus_plus = not_17_out ? 1'b0 : 1'bz;  // Controlled_Buffer controlled_buffer_27
  not not_17 (not_17_out, or_12_out);
  assign PC_plus_plus = or_12_out ? S : 1'bz;  // Controlled_Buffer controlled_buffer_28
  or or_12 (or_12_out, comparator_2_eq, demultiplexer_11_out1, demultiplexer_6_out1, demultiplexer_7_out1, demultiplexer_8_out1);
  assign DEC = not_18_out ? 1'b0 : 1'bz;  // Controlled_Buffer controlled_buffer_29
  not not_18 (not_18_out, demultiplexer_1_out1);
  assign DEC = demultiplexer_1_out1 ? S : 1'bz;  // Controlled_Buffer controlled_buffer_30
  assign AR_plus_plus = not_19_out ? 1'b0 : 1'bz;  // Controlled_Buffer controlled_buffer_31
  not not_19 (not_19_out, demultiplexer_9_out5);
  assign AR_plus_plus = demultiplexer_9_out5 ? S : 1'bz;  // Controlled_Buffer controlled_buffer_32
  assign DR_plus_plus = not_20_out ? 1'b0 : 1'bz;  // Controlled_Buffer controlled_buffer_33
  assign DR_plus_plus = demultiplexer_10_out6 ? S : 1'bz;  // Controlled_Buffer controlled_buffer_34
  not not_20 (not_20_out, demultiplexer_10_out6);
  assign CLA = not_21_out ? 1'b0 : 1'bz;  // Controlled_Buffer controlled_buffer_35
  not not_21 (not_21_out, demultiplexer_4_out0);
  assign CLA = demultiplexer_4_out0 ? S : 1'bz;  // Controlled_Buffer controlled_buffer_36
  assign CLE = not_22_out ? 1'b0 : 1'bz;  // Controlled_Buffer controlled_buffer_37
  not not_22 (not_22_out, demultiplexer_4_out1);
  assign CLE = demultiplexer_4_out1 ? S : 1'bz;  // Controlled_Buffer controlled_buffer_38
  assign LDAFALU2C = not_23_out ? 1'b0 : 1'bz;  // Controlled_Buffer controlled_buffer_39
  not not_23 (not_23_out, or_13_out);
  assign LDAFALU2C = or_13_out ? S : 1'bz;  // Controlled_Buffer controlled_buffer_40
  or or_13 (or_13_out, demultiplexer_4_out2, demultiplexer_4_out3, demultiplexer_4_out4, demultiplexer_4_out5, demultiplexer_4_out6);
  and and_4 (TMPS, 1'b0, S);
  and and_5 (TMPE, 1'b0, S);
  Demultiplexer #(.select(4), .disabled(0)) demultiplexer_4 (
    .out0(demultiplexer_4_out0), .out1(demultiplexer_4_out1), .out2(demultiplexer_4_out2),
    .out3(demultiplexer_4_out3), .out4(demultiplexer_4_out4), .out5(demultiplexer_4_out5),
    .out6(demultiplexer_4_out6), .out7(demultiplexer_4_out7), .out8(demultiplexer_4_out8),
    .out9(demultiplexer_4_out9), .out10(demultiplexer_4_out10), .out11(out_30), .in(demultiplexer_1_out0),
    .sel(table_1_out_2), .en(and_1_out));  // open: out12, out13, out14, out15
  Comparator #(.width(16)) comparator_12 (.a(in_4), .b({16{1'b0}}), .eq(comparator_12_eq));  // open: gt, lt
  Demultiplexer #(.disabled(0)) demultiplexer_5 (
    .out1(demultiplexer_5_out1), .in(demultiplexer_4_out10), .sel(not_25_out), .en(and_1_out));  // open: out0
  not not_24 (not_24_out, in_4[15]);
  not not_25 (not_25_out, in_5);
  Demultiplexer #(.disabled(0)) demultiplexer_6 (
    .out1(demultiplexer_6_out1), .in(demultiplexer_4_out7), .sel(not_24_out), .en(and_1_out));  // open: out0
  Demultiplexer #(.disabled(0)) demultiplexer_7 (
    .out1(demultiplexer_7_out1), .in(demultiplexer_4_out8), .sel(in_4[15]), .en(and_1_out));  // open: out0
  Demultiplexer #(.disabled(0)) demultiplexer_8 (
    .out1(demultiplexer_8_out1), .in(demultiplexer_4_out9), .sel(comparator_12_eq), .en(and_1_out));  // open: out0
  Demultiplexer #(.select(3), .disabled(0)) demultiplexer_9 (
    .out0(demultiplexer_9_out0), .out1(demultiplexer_9_out1), .out2(demultiplexer_9_out2),
    .out3(demultiplexer_9_out3), .out4(demultiplexer_9_out4), .out5(demultiplexer_9_out5),
    .out6(demultiplexer_9_out6), .in(demultiplexer_2_out0), .sel(in_7[14:12]), .en(not_7_out));  // open: out7
  Demultiplexer #(.select(3), .disabled(0)) demultiplexer_10 (
    .out0(demultiplexer_10_out0), .out1(demultiplexer_10_out1), .out2(demultiplexer_10_out2),
    .out3(demultiplexer_10_out3), .out4(demultiplexer_10_out4), .out5(demultiplexer_10_out5),
    .out6(demultiplexer_10_out6), .in(demultiplexer_3_out0), .sel(in_7[14:12]), .en(not_7_out));  // open: out7
  Comparator #(.width(16)) comparator_13 (.a(in_6), .b({16{1'b0}}), .eq(comparator_13_eq));  // open: gt, lt
  Comparator #(.width(3)) comparator_14 (.a(in_7[14:12]), .b(3'b110), .eq(comparator_14_eq));  // open: gt, lt
  Demultiplexer #(.disabled(0)) demultiplexer_11 (
    .out0(demultiplexer_11_out0), .out1(demultiplexer_11_out1), .in(comparator_7_eq), .sel(and_6_out),
    .en(not_7_out));
  and and_6 (and_6_out, comparator_13_eq, comparator_14_eq);

  assign out_31 = in_7;
  assign out_32 = in_7[14:12];

  // Notes on the sheet:
  //   ARE: pull=down
  //   ACE: pull=down
  //   ARS: pull=down
  //   IRE: pull=down
  //   MS: pull=down
  //   IRS: pull=down
  //   TMPS: pull=down
  //   ACS: pull=down
  //   PCE: pull=down
  //   ME: pull=down
  //   PCS: pull=down
  //   DRS: pull=down
endmodule

module CLOCK (
  input  in_1,
  output out_2,
  output out_3,
  output out_4
);

  wire j_k_ff_1_qn, nand_1_out;

  J_K_Flip_Flop j_k_ff_1 (.J(1'b1), .clk(in_1), .K(1'b1), .Q(out_2), .Qn(j_k_ff_1_qn));  // open: preset, en, reset
  nand nand_1 (nand_1_out, in_1, out_2);
  nand nand_2 (out_4, j_k_ff_1_qn, in_1);
  not not_1 (out_3, nand_1_out);
endmodule

module ALU1 (
  input  [15:0] in_1,
  input  [15:0] in_2,
  input  [2:0] in_3,
  input  in_4,
  input  in_5,
  input  in_6,
  input  [15:0] in_7,
  output [15:0] out_8,
  output out_9
);

  wire adder_1_cout, and_1_out, and_2_out, and_3_out, and_4_out, and_5_out, and_7_out, comparator_1_eq,
       comparator_2_eq, comparator_3_eq, comparator_4_eq, comparator_5_eq, comparator_6_eq, not_2_out;
  wire [15:0] adder_1_out, adder_2_out, and_6_out, multiplexer_1_out, not_1_out;
  wire [16:0] shifter_1_out, shifter_2_out;
  wire [16:16] controlled_buffer_1_out;

  Shifter #(.width(17), .shift("rr")) shifter_1 (.in({out_9, in_2}), .\dist (5'b00001), .out(shifter_1_out));
  Comparator #(.width(16)) comparator_1 (.a(in_7), .b(16'h7200), .eq(comparator_1_eq));  // open: gt, lt
  Comparator #(.width(16)) comparator_2 (.a(in_7), .b(16'h7100), .eq(comparator_2_eq));  // open: gt, lt
  Comparator #(.width(16)) comparator_3 (.a(in_7), .b(16'h7080), .eq(comparator_3_eq));  // open: gt, lt
  Comparator #(.width(16)) comparator_4 (.a(in_7), .b(16'h7040), .eq(comparator_4_eq));  // open: gt, lt
  Comparator #(.width(16)) comparator_5 (.a(in_7), .b(16'h7020), .eq(comparator_5_eq));  // open: gt, lt
  assign {controlled_buffer_1_out[16], out_8} = and_1_out ? shifter_1_out : 17'bz;  // Controlled_Buffer controlled_buffer_1
  Shifter #(.width(17), .shift("rl")) shifter_2 (.in({out_9, in_2}), .\dist (5'b00001), .out(shifter_2_out));
  and and_1 (and_1_out, in_6, comparator_3_eq);
  assign {controlled_buffer_1_out[16], out_8} = and_2_out ? shifter_2_out : 17'bz;  // Controlled_Buffer controlled_buffer_2
  and and_2 (and_2_out, in_6, comparator_4_eq);
  and and_3 (and_3_out, comparator_1_eq, in_6);
  and and_4 (and_4_out, comparator_2_eq, in_6);
  and and_5 (and_5_out, comparator_5_eq, in_6);
  Adder #(.width(16)) adder_1 (.a(in_1), .b(in_2), .out(adder_1_out), .cout(adder_1_cout));  // open: cin
  assign controlled_buffer_1_out[16] = and_7_out ? adder_1_cout : 1'bz;  // Controlled_Buffer controlled_buffer_3
  Adder #(.width(16)) adder_2 (.a(in_2), .b(16'h1), .out(adder_2_out));  // open: cin, cout
  assign and_6_out = in_1 & in_2;  // AND_Gate and_6, 16 bits wide
  assign not_1_out = ~in_2;  // NOT_Gate not_1, 16 bits wide
  assign out_8 = and_5_out ? adder_2_out : 16'bz;  // Controlled_Buffer controlled_buffer_4
  Comparator #(.width(3)) comparator_6 (.a(in_3), .b(3'b001), .eq(comparator_6_eq));  // open: gt, lt
  and and_7 (and_7_out, comparator_6_eq, in_4);
  assign out_8 = and_3_out ? not_1_out : 16'bz;  // Controlled_Buffer controlled_buffer_5
  not not_2 (not_2_out, out_9);
  assign controlled_buffer_1_out[16] = and_4_out ? not_2_out : 1'bz;  // Controlled_Buffer controlled_buffer_6
  Multiplexer #(.select(3), .width(16)) multiplexer_1 (
    .in0(and_6_out), .in1(adder_1_out), .in2(in_1), .in3(in_2), .out(multiplexer_1_out), .sel(in_3));  // open: in4, in5, in6, in7, en
  assign out_8 = in_4 ? multiplexer_1_out : 16'bz;  // Controlled_Buffer controlled_buffer_7
  Register #(.width(1), .trigger("falling")) register_1 (
    .D(controlled_buffer_1_out[16]), .Q(out_9), .clk(in_6), .clr(in_5));  // open: en

  // Notes on the sheet:
  //   AC+E
  //   DR
  //   AC
endmodule

module TABLE (
  input  [15:0] in_1,
  output [3:0] out_2
);

  wire comparator_1_eq, comparator_2_eq, comparator_3_eq, comparator_4_eq, comparator_5_eq, comparator_6_eq,
       comparator_7_eq, comparator_8_eq, comparator_9_eq, comparator_10_eq, comparator_11_eq,
       comparator_12_eq, not_1_out;
  wire [3:0] adder_1_out, adder_2_out, adder_3_out, adder_4_out, adder_5_out, adder_6_out, adder_7_out,
       adder_8_out, adder_9_out, adder_10_out, bit_extender_1_out, bit_extender_2_out, bit_extender_3_out,
       bit_extender_4_out, bit_extender_5_out, bit_extender_6_out, bit_extender_7_out, bit_extender_8_out,
       bit_extender_9_out, bit_extender_10_out, bit_extender_11_out, bit_extender_12_out;

  Comparator #(.width(16)) comparator_1 (.a(in_1), .b(16'h7800), .eq(comparator_1_eq));  // open: gt, lt
  Comparator #(.width(16)) comparator_2 (.a(in_1), .b(16'h7400), .eq(comparator_2_eq));  // open: gt, lt
  Comparator #(.width(16)) comparator_3 (.a(in_1), .b(16'h7200), .eq(comparator_3_eq));  // open: gt, lt
  Comparator #(.width(16)) comparator_4 (.a(in_1), .b(16'h7100), .eq(comparator_4_eq));  // open: gt, lt
  Comparator #(.width(16)) comparator_5 (.a(in_1), .b(16'h7080), .eq(comparator_5_eq));  // open: gt, lt
  Comparator #(.width(16)) comparator_6 (.a(in_1), .b(16'h7040), .eq(comparator_6_eq));  // open: gt, lt
  Comparator #(.width(16)) comparator_7 (.a(in_1), .b(16'h7020), .eq(comparator_7_eq));  // open: gt, lt
  Comparator #(.width(16)) comparator_8 (.a(in_1), .b(16'h7010), .eq(comparator_8_eq));  // open: gt, lt
  Comparator #(.width(16)) comparator_9 (.a(in_1), .b(16'h7008), .eq(comparator_9_eq));  // open: gt, lt
  Comparator #(.width(16)) comparator_10 (.a(in_1), .b(16'h7004), .eq(comparator_10_eq));  // open: gt, lt
  Comparator #(.width(16)) comparator_11 (.a(in_1), .b(16'h7002), .eq(comparator_11_eq));  // open: gt, lt
  Comparator #(.width(16)) comparator_12 (.a(in_1), .b(16'h7001), .eq(comparator_12_eq));  // open: gt, lt
  not not_1 (not_1_out, comparator_1_eq);
  assign bit_extender_1_out = {{3{not_1_out}}, not_1_out};  // Bit_Extender bit_extender_1
  assign bit_extender_2_out = {{3{1'b0}}, comparator_2_eq};  // Bit_Extender bit_extender_2
  assign bit_extender_3_out = {{3{1'b0}}, comparator_3_eq};  // Bit_Extender bit_extender_3
  assign bit_extender_4_out = {{3{1'b0}}, comparator_4_eq};  // Bit_Extender bit_extender_4
  assign bit_extender_5_out = {{3{1'b0}}, comparator_5_eq};  // Bit_Extender bit_extender_5
  assign bit_extender_6_out = {{3{1'b0}}, comparator_6_eq};  // Bit_Extender bit_extender_6
  assign bit_extender_7_out = {{3{1'b0}}, comparator_7_eq};  // Bit_Extender bit_extender_7
  assign bit_extender_8_out = {{3{1'b0}}, comparator_8_eq};  // Bit_Extender bit_extender_8
  assign bit_extender_9_out = {{3{1'b0}}, comparator_9_eq};  // Bit_Extender bit_extender_9
  assign bit_extender_10_out = {{3{1'b0}}, comparator_10_eq};  // Bit_Extender bit_extender_10
  assign bit_extender_11_out = {{3{1'b0}}, comparator_11_eq};  // Bit_Extender bit_extender_11
  assign bit_extender_12_out = {{3{1'b0}}, comparator_12_eq};  // Bit_Extender bit_extender_12
  assign out_2 = comparator_1_eq ? bit_extender_1_out : 4'bz;  // Controlled_Buffer controlled_buffer_1
  assign out_2 = comparator_2_eq ? bit_extender_2_out : 4'bz;  // Controlled_Buffer controlled_buffer_2
  Adder #(.width(4)) adder_1 (.a(bit_extender_3_out), .b(4'b0001), .out(adder_1_out));  // open: cin, cout
  Adder #(.width(4)) adder_2 (.a(bit_extender_4_out), .b(4'b0010), .out(adder_2_out));  // open: cin, cout
  Adder #(.width(4)) adder_3 (.a(bit_extender_5_out), .b(4'b0011), .out(adder_3_out));  // open: cin, cout
  Adder #(.width(4)) adder_4 (.a(bit_extender_6_out), .b(4'b0100), .out(adder_4_out));  // open: cin, cout
  Adder #(.width(4)) adder_5 (.a(bit_extender_7_out), .b(4'b0101), .out(adder_5_out));  // open: cin, cout
  Adder #(.width(4)) adder_6 (.a(bit_extender_8_out), .b(4'b0110), .out(adder_6_out));  // open: cin, cout
  Adder #(.width(4)) adder_7 (.a(bit_extender_9_out), .b(4'b0111), .out(adder_7_out));  // open: cin, cout
  Adder #(.width(4)) adder_8 (.a(bit_extender_10_out), .b(4'b1000), .out(adder_8_out));  // open: cin, cout
  Adder #(.width(4)) adder_9 (.a(bit_extender_11_out), .b(4'b1001), .out(adder_9_out));  // open: cin, cout
  Adder #(.width(4)) adder_10 (.a(bit_extender_12_out), .b(4'b1010), .out(adder_10_out));  // open: cin, cout
  assign out_2 = comparator_3_eq ? adder_1_out : 4'bz;  // Controlled_Buffer controlled_buffer_3
  assign out_2 = comparator_4_eq ? adder_2_out : 4'bz;  // Controlled_Buffer controlled_buffer_4
  assign out_2 = comparator_5_eq ? adder_3_out : 4'bz;  // Controlled_Buffer controlled_buffer_5
  assign out_2 = comparator_6_eq ? adder_4_out : 4'bz;  // Controlled_Buffer controlled_buffer_6
  assign out_2 = comparator_7_eq ? adder_5_out : 4'bz;  // Controlled_Buffer controlled_buffer_7
  assign out_2 = comparator_8_eq ? adder_6_out : 4'bz;  // Controlled_Buffer controlled_buffer_8
  assign out_2 = comparator_9_eq ? adder_7_out : 4'bz;  // Controlled_Buffer controlled_buffer_9
  assign out_2 = comparator_10_eq ? adder_8_out : 4'bz;  // Controlled_Buffer controlled_buffer_10
  assign out_2 = comparator_11_eq ? adder_9_out : 4'bz;  // Controlled_Buffer controlled_buffer_11
  assign out_2 = comparator_12_eq ? adder_10_out : 4'bz;  // Controlled_Buffer controlled_buffer_12
endmodule

module PC (
  input  in_1,
  input  [11:0] in_2,
  input  in_3,
  input  in_4,
  input  in_5,
  input  in_6,
  output [11:0] out_7,
  output [11:0] out_8
);

  wire [11:0] adder_1_out, controlled_buffer_1_out, controlled_buffer_2_out;

  assign controlled_buffer_1_out = in_1 ? out_7 : 12'bz;  // Controlled_Buffer controlled_buffer_1
  Adder #(.width(12)) adder_1 (.a(controlled_buffer_1_out), .b(12'h1), .out(adder_1_out));  // open: cin, cout
  assign controlled_buffer_2_out = in_5 ? in_2 : 12'bz;  // Controlled_Buffer controlled_buffer_2
  assign controlled_buffer_2_out = in_1 ? adder_1_out : 12'bz;  // Controlled_Buffer controlled_buffer_3
  Register #(.width(12), .trigger("falling")) register_1 (
    .D(controlled_buffer_2_out), .Q(out_7), .clk(in_3), .clr(in_4));  // open: en
  assign out_8 = in_6 ? out_7 : 12'bz;  // Controlled_Buffer controlled_buffer_4

  // Notes on the sheet:
  //   in_2: pull=down
  //   in_5: pull=down
  //   in_6: pull=down
  //   in_4: pull=down
endmodule

module IR (
  input  in_1,
  input  [15:0] in_2,
  input  in_3,
  input  in_4,
  input  in_5,
  input  in_6,
  output [15:0] out_7,
  output [15:0] out_8
);

  wire [15:0] controlled_buffer_1_out, controlled_buffer_2_out, subtractor_1_out;

  Subtractor #(.width(16)) subtractor_1 (
    .a(controlled_buffer_2_out), .b(16'h8000), .out(subtractor_1_out));  // open: bin, bout
  assign controlled_buffer_1_out = in_3 ? in_2 : 16'bz;  // Controlled_Buffer controlled_buffer_1
  assign controlled_buffer_2_out = in_1 ? out_7 : 16'bz;  // Controlled_Buffer controlled_buffer_2
  assign controlled_buffer_1_out = in_1 ? subtractor_1_out : 16'bz;  // Controlled_Buffer controlled_buffer_3
  Register #(.width(16), .trigger("falling")) register_1 (
    .D(controlled_buffer_1_out), .Q(out_7), .clk(in_4), .clr(in_5));  // open: en
  assign out_8 = in_6 ? out_7 : 16'bz;  // Controlled_Buffer controlled_buffer_4

  // Notes on the sheet:
  //   in_1: pull=down
  //   in_6: pull=down
  //   in_5: pull=down
endmodule

module AR (
  input  in_1,
  input  [11:0] in_2,
  input  in_3,
  input  in_4,
  input  in_5,
  input  in_6,
  output [11:0] out_7,
  output [11:0] out_8
);

  wire [11:0] adder_1_out, controlled_buffer_1_out, controlled_buffer_3_out;

  Adder #(.width(12)) adder_1 (.a(controlled_buffer_3_out), .b(12'h1), .out(adder_1_out));  // open: cin, cout
  assign controlled_buffer_1_out = in_1 ? adder_1_out : 12'bz;  // Controlled_Buffer controlled_buffer_1
  assign controlled_buffer_1_out = in_4 ? in_2 : 12'bz;  // Controlled_Buffer controlled_buffer_2
  assign controlled_buffer_3_out = in_1 ? out_7 : 12'bz;  // Controlled_Buffer controlled_buffer_3
  Register #(.width(12), .trigger("falling")) register_1 (
    .D(controlled_buffer_1_out), .Q(out_7), .clk(in_3), .clr(in_5));  // open: en
  assign out_8 = in_6 ? out_7 : 12'bz;  // Controlled_Buffer controlled_buffer_4

  // Notes on the sheet:
  //   in_4: pull=down
  //   in_5: pull=down
  //   in_2: pull=down
  //   in_6: pull=down
endmodule

module AC (
  input  [15:0] in_1,
  input  [15:0] in_2,
  input  in_3,
  input  in_4,
  input  in_5,
  input  in_6,
  output [15:0] out_7,
  output [15:0] out_8
);

  wire [15:0] controlled_buffer_1_out, multiplexer_1_out;

  assign controlled_buffer_1_out = in_5 ? in_2 : 16'bz;  // Controlled_Buffer controlled_buffer_1
  Multiplexer #(.width(16)) multiplexer_1 (
    .in0(in_1), .in1(controlled_buffer_1_out), .out(multiplexer_1_out), .sel(in_5));  // open: en
  Register #(.width(16), .trigger("falling")) register_1 (
    .D(multiplexer_1_out), .Q(out_7), .clk(in_3), .clr(in_4));  // open: en
  assign out_8 = in_6 ? out_7 : 16'bz;  // Controlled_Buffer controlled_buffer_2

  // Notes on the sheet:
  //   in_6: pull=down
  //   in_4: pull=down
endmodule

module TMP (
  input  [15:0] in_1,
  input  in_2,
  input  in_3,
  input  in_4,
  output [15:0] out_5,
  output [15:0] out_6
);

  wire [15:0] controlled_buffer_1_out;

  assign controlled_buffer_1_out = in_3 ? in_1 : 16'bz;  // Controlled_Buffer controlled_buffer_1
  Register #(.width(16), .trigger("falling")) register_1 (
    .D(controlled_buffer_1_out), .Q(out_5), .clk(in_4));  // open: en, clr
  assign out_6 = in_2 ? out_5 : 16'bz;  // Controlled_Buffer controlled_buffer_2

  // Notes on the sheet:
  //   out_6: pull=down
  //   in_1: pull=down
  //   out_5: pull=down
endmodule
